# Fritzing sketch Fritzing diagram (saved by Fritzing 0.9.10b)
breadboards: 1

parts:
  Part1 = Adafruit HUZZAH32 ESP32 Feather [part_number="Adafruit #3405"]
  LED1 = LED - 5mm [color="Red (633nm)" current=0.030 package="5 mm [THT]"]
  J1 = Basic Servo
  LED2 = LED - 5mm [color="Green (555nm)" current=0.030 package="5 mm [THT]"]
  HC-SR04_Sensor_1 = HC-SR04 Ultrasonic Distance Sensor
  Part2 = RFID-RC522-v3
  S1 = Pushbutton [package="[THT]"]
  BAT1 = Battery Holders [package=lipo-1100mAh]  # not connected
  Part3 = Adafruit Radio FeatherWing [part_number="Adafruit #3229, 3230, 3231, 3232"]
  ANT1 = Antenna  # not connected

nets:
  N1: Part1.IO21, Part3.RF_RST
  N2: Part1.IO17, Part3.RX
  N3: Part1.IO16, Part3.TX
  N4: Part1.MISO, Part2.MISO
  N5: Part1.MOSI, Part2.MOSI
  N6: Part1.SCK, Part2.SCK
  N7: Part1.A5_IO4, S1.Pin_2
  GND: Part1.GND, LED1.cathode, J1.gnd, LED2.cathode, HC-SR04_Sensor_1.GND, Part2.GND, Part3.GND
  3.3V: Part1.3.3V, HC-SR04_Sensor_1.VCC, Part2.3.3V, Part3.3.3V
  N8: Part1.VBAT, J1.vcc, S1.Pin_3
  N9: Part1.IO13_A12, J1.pulse
  N10: Part1.IO12_A11, HC-SR04_Sensor_1.TRIG
  N11: Part1.IO27_A10, LED2.anode
  N12: Part1.IO33_A9, LED1.anode
  N13: Part1.IO15_A8, Part2.SDA
  N14: Part1.IO32_A7, Part2.RST
  N15: Part1.IO14_A6, HC-SR04_Sensor_1.ECHO

notes:
  R2483
  Lora Module via serial

custom parts:
  RFID-RC522-v3: A simple China made RFID-RC522 Reader (6x4 cm); do check the pin labels, as this is a MFRC522 based clone.
  Adafruit Radio FeatherWing: Add short-hop wireless to your Feather with these Radio Featherwings. These add-ons for any Feather board will let you integrate packetized radio (with the RFM69 radio) or LoRa radio (with the RFM9x's). These radios are good options for kilometer-range radio, and paired with one of our WiFi, cellular or Bluetooth Feathers, will let you bridge from 433/900 MHz to the Internet or your mobile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
